# Fritzing sketch memorygame (saved by Fritzing 0.9.3b)
breadboards: 1

parts:
  LED1 = smd LED [color="Green (560nm)" package="0603 [SMD]"]
  LED2 = smd LED [color="Yellow (585nm)" package="0603 [SMD]"]
  LED3 = smd LED [color="Blue (470nm)" package="0603 [SMD]"]
  LED4 = smd LED [color="Red (633nm)" package="0603 [SMD]"]
  S1 = Pushbutton [package="[SMD]"]
  S2 = Pushbutton [package="[SMD]"]
  S3 = Pushbutton [package="[SMD]"]
  S4 = Pushbutton [package="[SMD]"]
  J1 = Piezo Speaker
  Bauteil2 = Arduino Nano (Rev3.0)

nets:
  N1: LED1.cathode, LED2.cathode, LED3.cathode, LED4.cathode, S1.Pin_1, S1.Pin_2, S2.Pin_1, S2.Pin_2, S3.Pin_1, S3.Pin_2, S4.Pin_1, S4.Pin_2, J1.pin1, Bauteil2.GND
  N2: LED1.anode, Bauteil2.D9
  N3: LED2.anode, Bauteil2.D10
  N4: LED3.anode, Bauteil2.D11/MOSI
  N5: LED4.anode, Bauteil2.D12/MISO
  N6: S1.Pin_3, S1.Pin_4, Bauteil2.D5
  N7: S2.Pin_3, S2.Pin_4, Bauteil2.D4
  N8: S3.Pin_3, S3.Pin_4, Bauteil2.D3
  N9: S4.Pin_3, S4.Pin_4, Bauteil2.D2
  N10: J1.pin2, Bauteil2.D6
